# Fritzing sketch RPi-OLED (saved by Fritzing 0.9.1b)

parts:
  electronicsguy1 = electronicsguy 0.96" 128x64 SPI I2C OLED
  Raspberry_Pi1 = Raspberry Pi B+

nets:
  VCC: electronicsguy1.VCC, Raspberry_Pi1.5V
  GND: electronicsguy1.GND, Raspberry_Pi1.GND
  N1: electronicsguy1.D1, Raspberry_Pi1.GPIO10
  N2: electronicsguy1.D0, Raspberry_Pi1.GPIO11

custom parts:
  electronicsguy 0.96" 128x64 SPI I2C OLED: Generic 0.96" 128x64 SPI I2C OLED Default is SPI mode Can be re-configured for I2C (needs soldering work) Comes in various colors like blue, white, yellow-blue
